# Fritzing sketch iot-power-meter (saved by Fritzing 1.0.0d)
breadboards: 1

parts:
  Orange_Pi_One1 = Orange Pi One [part_number=OPI-ONE]
  C1 = Capacitor Polarized [package=cpol-radial-10uf-25v]
  R1 = Resistor [tolerance=±5% resistance=100k package="0402 [SMD]"]
  R2 = Resistor [tolerance=±5% resistance=100k package="0402 [SMD]"]
  Display1 = LCD screen 16x2 IIC [part_number=101290]
  ADC1 = MCP3008 [package=dil16]
  KY-1 = Keyes Relay [package=THT]

nets:
  3V3: Orange_Pi_One1.3v3, Display1.VCC
  N1: Orange_Pi_One1.PA12, Display1.SDA
  N2: Orange_Pi_One1.PA11, Display1.SCL
  N3: Orange_Pi_One1.PA6, KY-1.signal
  GND: Orange_Pi_One1.GND, C1.-, R1.Pin_0, Display1.GND, ADC1.DGND, ADC1.AGND, KY-1.ground
  N4: Orange_Pi_One1.PA1, ADC1.Dout
  N5: Orange_Pi_One1.PA0, ADC1.Din
  N6: Orange_Pi_One1.PC2, ADC1.CLK
  N7: Orange_Pi_One1.PC3, ADC1.CS/SHDN
  5V: Orange_Pi_One1.5V, R2.Pin_1, ADC1.VREF, ADC1.VDD, KY-1.power
  N8: C1.+, R1.Pin_1, R2.Pin_0

custom parts:
  Orange Pi One: It’s an open-source single-board computer. It can run Android 4.4, Ubuntu, Debian, Rasberry Pi Image, as well as the banana pi Image. It uses the AllWinner H3 SoC, and has 512MB DDR3 SDRAM
  LCD screen 16x2 IIC: LCD screen with HD44780 controller enables showing text, symbols, value or anything else that comes from Croduino/Arduino. It is capable of showing 16 symbols in two lines and therefore can be used in many projects that need to send clearly visible and legible output information.. • Color of symbols: White • Backlight: Blue • Dimensions: 80 x 36 x 12 mm • Screen dimensions: 64.5 x 16 mm •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
  Keyes Relay: The Keyes 5V relay module is suitable for SCM development, home appliance control. It uses a 5V~12V TIL control signal which can control DC / AC signal.
